// Digital circuit 26bitcounter.dig as structural Verilog
module _26bitcounter (
  input  INPUT,
  input  SET,
  input  CLK,
  output Q0,
  output Q1,
  output Q2,
  output Q3,
  output Q4
);

  wire and_1_out;

  JK_FF_AS F0 (.Set(SET), .J(INPUT), .C(CLK), .K(INPUT), .Clr(and_1_out), .Q(Q0));  // open: nQ
  JK_FF_AS F1 (.Set(SET), .J(Q0), .C(CLK), .K(Q0), .Clr(and_1_out), .Q(Q1));  // open: nQ
  JK_FF_AS F2 (.Set(SET), .J(Q1), .C(CLK), .K(Q1), .Clr(and_1_out), .Q(Q2));  // open: nQ
  JK_FF_AS F3 (.Set(SET), .J(Q2), .C(CLK), .K(Q2), .Clr(and_1_out), .Q(Q3));  // open: nQ
  and and_1 (and_1_out, ~Q4, ~Q3, Q2, ~Q1, Q0);  // And
  JK_FF_AS F4 (.Set(SET), .J(Q3), .C(CLK), .K(Q3), .Clr(and_1_out), .Q(Q4));  // open: nQ

  // Notes on the sheet:
  //   INPUT: Hz: 5000
  //   CLK: Hz: 5000
endmodule
