// Digital circuit fafaf.dig as structural Verilog
module fafaf (
  input  [2:0] in_1,
  input  in_3,
  input  [1:0] in_4,
  input  in_6,
  input  [3:0] in_7,
  input  [3:0] in_9,
  input  [1:0] in_10,
  input  clk,
  input  in_13,
  input  in_14,
  input  [15:0] in_17,
  input  [2:0] in_26,
  output [7:0] out_2,
  output [3:0] out_5,
  output [6:0] out_8,
  output out_11,
  output out_15,
  output [3:0] out_16,
  output [15:0] out_18,
  output [15:0] out_19,
  output [15:0] out_20,
  output [15:0] out_21,
  output [15:0] out_22,
  output [15:0] out_23,
  output [15:0] out_24,
  output [15:0] out_25
);

  bc7seg #(.applicationType("GHDL")) u_bc7seg (.EN(in_6), .D(in_7), .S(out_8));
  decoder_to8 #(.applicationType("GHDL")) u_decoder_to8 (.A(in_1), .Y(out_2));
  decoder2to4 #(.applicationType("GHDL")) u_decoder2to4 (.EN(in_3), .A(in_4), .Y_L(out_5));
  mux #(.applicationType("GHDL")) u_mux (.I(in_9), .SEL(in_10), .Y(out_11));
  decoder1to8 #(.applicationType("GHDL")) u_decoder1to8 (
    .A(in_17), .SEL(in_26), .S0(out_18), .S1(out_19), .S2(out_20), .S3(out_21), .S4(out_22), .S5(out_23),
    .S6(out_24), .S7(out_25));
  counterto9 #(.applicationType("GHDL")) u_counterto9 (
    .enable(in_13), .clock(clk), .reset(in_14), .ov(out_15), .count(out_16));
endmodule

/* Code of bc7seg:
LIBRARY ieee;
USE ieee.std_logic_1164.all;


ENTITY bc7seg IS 
    PORT(
        EN: IN STD_LOGIC;
        D: IN STD_LOGIC_VECTOR (3 DOWNTO 0);
        S: OUT STD_LOGIC_VECTOR (6 DOWNTO 0)
    );
END ENTITY bc7seg;


ARCHITECTURE behavioral OF bc7seg IS 
BEGIN 
    PROCESS(EN,D)
    BEGIN 
        IF EN = '0' THEN
            S <= "0000000";
        ELSE 
            CASE D IS 
                WHEN "0000" => S <= "1111110";
                WHEN "0001" => S <=  "0110000";
                WHEN "0010" => S <=  "1101101";
                WHEN "0011" => S <=  "1111001";
                WHEN "0100" => S <=  "0110011";
                WHEN "0101" => S <=  "1011011";
                WHEN "0110" => S <=  "1011111";
                WHEN "0111" => S <=  "1110000";
                WHEN "1000" => S <=  "1111111";
                WHEN "1001" => S <=  "1111011";
                WHEN OTHERS => NULL;
            END CASE;
        END IF;
    END PROCESS;
END ARCHITECTURE;
*/

/* Code of decoder_to8:
-- 1 - Projete e descreva em VHDL um decodificador 3 para 8. Utilize a seguinte entidade para
-- descrever sua solução em VHDL:


LIBRARY ieee;
USE ieee.std_logic_1164.all;


ENTITY decoder_to8 IS 
    PORT (
        A: IN STD_LOGIC_VECTOR(2 DOWNTO 0);
        Y: OUT STD_LOGIC_VECTOR(7 DOWNTO 0)
    );
END ENTITY;


ARCHITECTURE behavioral OF decoder_to8 IS 
BEGIN 
    PROCESS(A)
    BEGIN 
        Y <= "00000000";
        CASE A IS 
            WHEN "000" => Y(0) <= '1';
            WHEN "001" => Y(1) <= '1'; 
            WHEN "010" => Y(2) <= '1';
            WHEN "011" => Y(3) <= '1';
            WHEN "100" => Y(4) <= '1';
            WHEN "101" => Y(5) <= '1';
            WHEN "110" => Y(6) <= '1';
            WHEN "111" => Y(7) <= '1';
            WHEN OTHERS => NULL;
        END CASE;
    END PROCESS;
END ARCHITECTURE;
*/

/* Code of decoder2to4:
LIBRARY IEEE;
USE ieee.std_logic_1164.all;



ENTITY decoder2to4 IS 
    PORT (
        EN: IN STD_LOGIC;
        A: IN STD_LOGIC_VECTOR(1 DOWNTO 0);
        Y_L: OUT STD_LOGIC_VECTOR(3 DOWNTO 0)
    );
END ENTITY;

ARCHITECTURE behavioral of decoder2to4 IS
BEGIN
    PROCESS(EN,A)
    BEGIN 
        Y_L <= "0000";
        IF EN = '1' THEN
            CASE A IS
                WHEN "00" => Y_L(0) <= '1';
                WHEN "01" => Y_L(1) <= '1';
                WHEN "10" => Y_L(2) <= '1';
                WHEN "11" => Y_L(3) <= '1';
                WHEN OTHERS => NULL;
            END CASE;
         ELSE 
            Y_L <= "0000";
        END IF;
    END PROCESS;    
END ARCHITECTURE;
*/

/* Code of mux:
LIBRARY ieee;
USE ieee.std_logic_1164.all;

ENTITY mux IS
    PORT (
        I: IN STD_LOGIC_VECTOR(3 DOWNTO 0);
        SEL: IN STD_LOGIC_VECTOR(1 DOWNTO 0);
        Y: OUT STD_LOGIC
    );
END ENTITY mux;

ARCHITECTURE behavioral OF mux IS 
BEGIN 
    PROCESS(I, SEL)
    BEGIN 
        CASE SEL IS 
            WHEN "00" => Y <= I(0);
            WHEN "01" => Y <= I(1);
            WHEN "10" => Y <= I(2);
            WHEN "11"  => Y <= I(3);
	    WHEN OTHERS => Y <= '0';
        END CASE;
    END PROCESS;
END ARCHITECTURE;
*/

/* Code of decoder1to8:
LIBRARY ieee;
    USE ieee.std_logic_1164.all;


    ENTITY decoder1to8 IS 
        PORT(
            A : IN STD_LOGIC_VECTOR(15 DOWNTO 0);
            SEL : IN STD_LOGIC_VECTOR(2 DOWNTO 0);
            S0 : OUT STD_LOGIC_VECTOR(15 DOWNTO 0);
            S1 : OUT STD_LOGIC_VECTOR(15 DOWNTO 0);
            S2 : OUT STD_LOGIC_VECTOR(15 DOWNTO 0);
            S3 : OUT STD_LOGIC_VECTOR(15 DOWNTO 0);
            S4 : OUT STD_LOGIC_VECTOR(15 DOWNTO 0);
            S5 : OUT STD_LOGIC_VECTOR(15 DOWNTO 0);
            S6 : OUT STD_LOGIC_VECTOR(15 DOWNTO 0);
            S7 : OUT STD_LOGIC_VECTOR(15 DOWNTO 0)
        );
    END ENTITY decoder1to8; 


    ARCHITECTURE behavioral of decoder1to8 IS 
    BEGIN 
        PROCESS(A, SEL)
            BEGIN
            S0 <= "0000000000000000";
            S1 <= "0000000000000000";
            S2 <= "0000000000000000";
            S3 <= "0000000000000000";
            S4 <= "0000000000000000";
            S5 <= "0000000000000000";
            S6 <= "0000000000000000";
            S7 <= "0000000000000000";
            CASE SEL IS 
                WHEN "000" => S0 <= A;
                WHEN "001" => S1 <= A;
                WHEN "010" => S2 <= A;
                WHEN "011" => S3 <= A;
                WHEN "100" => S4 <= A;
                WHEN "101" => S5 <= A;
                WHEN "110" => S6 <= A;
                WHEN "111" => S7 <= A;
                WHEN OTHERS => NULL;
            END CASE;
        END PROCESS;
    END ARCHITECTURE behavioral;
*/

/* Code of counterto9:
LIBRARY ieee;
USE ieee.std_logic_1164.all;


ENTITY counterto9 IS
    PORT(
        enable: IN STD_LOGIC;
        clock: IN STD_LOGIC;
        reset: IN STD_LOGIC;
        ov: OUT STD_LOGIC;
        count: OUT STD_LOGIC_VECTOR(3 DOWNTO 0)
    );
END ENTITY counterto9;

ARCHITECTURE behavioral OF counterto9 IS 

signal current : std_logic_vector(3 DOWNTO 0);
signal change : std_logic;
BEGIN   
    PROCESS(CLOCK, ENABLE, RESET, CURRENT)
    BEGIN   
    
    IF enable = '1' THEN
        CASE RESET IS
            WHEN '1' => current <= "0000";
            WHEN OTHERS => NULL;
        END CASE;
        IF rising_edge(clock) THEN
            CASE CURRENT IS
                WHEN "0000" =>  current <= "0001";
                WHEN "0001" => current <= "0010";
                WHEN "0010" => current <= "0011";
                WHEN "0011" => current <= "0100";
                WHEN "0100" => current <= "0101";
                WHEN "0101" => current <= "0110";
                WHEN "0110" => current <= "0111";
                WHEN "0111" => current <= "1000";
                WHEN "1000" => current <= "1001";
                WHEN "1001" =>
                    current <= "0000";
                    change <= '1';
                WHEN OTHERS => NULL;
            END CASE;
        END IF;
    ELSE 
        current <= "0000";
    END IF;
    END PROCESS;
    count <= current;
    ov <= change;
END ARCHITECTURE;
*/
