// Digital circuit exerciciofaf.dig as structural Verilog
module exerciciofaf (
  input  in_1,
  input  in_2,
  input  in_3,
  input  in_4,
  input  [3:0] in_6,
  input  in_8,
  input  in_9,
  input  in_10,
  input  in_14,
  input  in_15,
  input  in_16,
  input  [2:0] in_20,
  input  in_21,
  input  in_22,
  input  in_23,
  input  in_24,
  output out_5,
  output out_7,
  output out_11,
  output out_12,
  output out_13,
  output out_17,
  output out_18,
  output [7:0] out_19
);

  wire u_full_adder_2_cout, u_full_adder_cout, u_full_adder_s, undriven;

  schematic1 #(.applicationType("GHDL")) u_schematic1 (
    .a(in_8), .b(in_9), .c(in_10), .d(out_13), .e(out_12), .f(out_11));
  four_arrayor #(.applicationType("GHDL")) u_four_arrayor (.a(in_6), .s(out_7));
  four_entryor #(.applicationType("GHDL")) u_four_entryor (.a(in_1), .b(in_2), .c(in_3), .d(in_4), .s(out_5));
  schematic2 #(.applicationType("GHDL")) u_schematic2 (.a(in_14), .b(in_15), .c(in_16), .d(out_17), .e(out_18));
  decoder_3to8 #(.applicationType("GHDL")) u_decoder_3to8 (.a(in_20), .y(out_19));
  half_adder #(.applicationType("GHDL")) u_half_adder (.a(in_21), .b(in_22));  // open: s, cout
  full_adder #(.applicationType("GHDL")) u_full_adder (
    .a(undriven), .b(in_24), .s(u_full_adder_s), .cout(u_full_adder_cout));
  full_adder #(.applicationType("GHDL")) u_full_adder_2 (
    .a(in_23), .b(u_full_adder_s), .cout(u_full_adder_2_cout));  // open: s
  // Or or_1 has open pins: In_1=u_full_adder_cout, In_2=u_full_adder_2_cout, out=open
endmodule

/* Code of schematic1:
library ieee;
use ieee.std_logic_1164.all;

ENTITY schematic1 IS
    port(
        a: IN STD_LOGIC; 
        b: IN STD_LOGIC;
        c: IN STD_LOGIC;
        d, e, f: OUT STD_LOGIC
    );
END schematic1;


ARCHITECTURE behaviour_or OF schematic1 IS 
BEGIN
    d <= (not a) and b;
    e <= '1';
    f <= (not b) and (not c);
END behaviour_or;
*/

/* Code of four_arrayor:
library ieee;
use ieee.std_logic_1164.all;

ENTITY four_arrayor IS 
    PORT (
        a: IN STD_LOGIC_VECTOR(3 downto 0);
        s: OUT STD_LOGIC
    );
END four_arrayor;

ARCHITECTURE behaviour_or OF four_arrayor IS 
BEGIN
    s <= a(0) OR a(1) OR a(2) OR a(3);
END behaviour_or;
*/

/* Code of four_entryor:
library ieee;
    use ieee.std_logic_1164.all;

    ENTITY four_entryor IS
        port(
            a: IN STD_LOGIC; 
            b: IN STD_LOGIC;
            c: IN STD_LOGIC;
            d: IN STD_LOGIC;
            s: OUT STD_LOGIC
        );
    END four_entryor;


    ARCHITECTURE behaviour_or OF four_entryor IS 
    BEGIN
        S <= a OR b OR c OR d;
    END behaviour_or;
*/

/* Code of schematic2:
LIBRARY ieee;
USE ieee.std_logic_1164.all;

ENTITY schematic2 IS 
    PORT (
        a: IN STD_LOGIC;
        b: IN STD_LOGIC;
        c: IN STD_LOGIC;
        d, e: OUT STD_LOGIC
    );
END schematic2;

ARCHITECTURE behaviour OF schematic2 IS 
BEGIN 
    d <= ((not a) and c) or (not a and b) or (b and c);
    e <= (not a and not b and c) or (not a and b and not c) or (a and not b and not c) or (a and b and c);
END behaviour;
*/

/* Code of decoder_3to8:
-- O código não funcionou de jeito nenhum, nem fazendo de outros modos,
-- incluindo pedindo pra chatgpt, entre outros. Talvez meu digital
-- esteja com problema

-- O problema só acontece com BIT_VECTOR
-- Então fiz a questão com STD_LOGIC_VECTOR


library ieee;
use ieee.std_logic_1164.all;


ENTITY decoder_3to8 IS 
    PORT (
        a : IN STD_LOGIC_VECTOR(2 DOWNTO 0);  
        y : OUT STD_LOGIC_VECTOR(7 DOWNTO 0)  
    );
END decoder_3to8;

ARCHITECTURE behaviour OF decoder_3to8 IS 
BEGIN 
    y(0) <= not a(2) and not a(1) and not a(0);  -- 000
    y(1) <= not a(2) and not a(1) and a(0);     -- 001
    y(2) <= not a(2) and a(1) and not a(0);     -- 010
    y(3) <= not a(2) and a(1) and a(0);        -- 011
    y(4) <= a(2) and not a(1) and not a(0);     -- 100
    y(5) <= a(2) and not a(1) and a(0);        -- 101
    y(6) <= a(2) and a(1) and not a(0);        -- 110
    y(7) <= a(2) and a(1) and a(0);            -- 111
END behaviour;
*/

/* Code of half_adder:
library ieee;
use ieee.std_logic_1164.all;


entity half_adder is 
    port (
      a, b : in std_logic;
      s, cout : out std_logic
    );
end half_adder;

architecture behavioral of half_adder is 
begin 
  s <= a xor b;
  cout <= a and b;
end behavioral;

library ieee;
use ieee.std_logic_1164.all;

entity full_adder is 
    port (
      a,b, cin: in std_logic;
      s, cout: out std_logic
    );
end full_adder;

architecture behavioral of full_adder is 
  signal e,f: std_logic;
  begin
  e <=  a xor b;
  s <= e xor cin;
  f <= a and b;
  cout <= (a and b) or (cin and e);
end behavioral;
*/

/* Code of full_adder:
library ieee;
use ieee.std_logic_1164.all;


entity half_adder is 
    port (
      a, b : in std_logic;
      s, cout : out std_logic
    );
end half_adder;

architecture behavioral of half_adder is 
begin 
  s <= a xor b;
  cout <= a and b;
end behavioral;

library ieee;
use ieee.std_logic_1164.all;

entity full_adder is 
    port (
      a,b, cin: in std_logic;
      s, cout: out std_logic
    );
end full_adder;

architecture behavioral of full_adder is 
  signal e,f: std_logic;
  begin
  e <=  a xor b;
  s <= e xor cin;
  f <= a and b;
  cout <= (a and b) or (cin and e);
end behavioral;
*/
